// Logisim project 8_bit_v01.circ as structural Verilog: 1 circuit, main circuit main
module main (
);

  wire CARRY, CLK, IX_OUT, LOAD_ALU, LOAD_FLAGS, LOAD_IR, LOAD_IX, LOAD_PC, LOAD_REGA, LOAD_REGB, or_1_out,
       PC_OUT, PCP1_OUT, RAM_OE, RAM_WE, REGA_OUT, REGB_OUT, RESET, RESET_CTR, ZERO;
  wire [1:0] counter_1_q;
  wire [3:0] ALU_MODE;
  wire [7:0] adder_1_out, adder_2_out, ADDR_BUS, ALU_OUT, DATA_BUS, divider_1_out, IX_q, multiplexer_2_out,
       multiplier_1_out, PC_q, ram_1_dout, REGA_DATA, REGB_DATA, STATUS_FLAGS_q, subtractor_1_out;
  wire [11:0] counter_2_q;
  wire [19:13] cpu_logic_out;

  Clock u_CLK (.out(CLK));
  Counter #(.max('h3), .ongoal("stay"), .width(2)) counter_1 (
    .clr(1'b0), .load(1'b0), .up(1'b1), .count(1'b1), .clk(CLK), .Q(counter_1_q));  // open: D, carry
  Adder adder_1 (.a(PC_q), .b(8'h1), .out(adder_1_out));  // open: cin, cout
  // Digital_Oscilloscope digital_oscilloscope_1: pin names not known; wires that end beside it: CLK
  Register PC (.D(adder_1_out), .en(LOAD_PC), .clk(CLK), .Q(PC_q), .clr(RESET));
  assign ADDR_BUS = PCP1_OUT ? adder_1_out : 8'bz;  // Controlled_Buffer controlled_buffer_1
  assign ADDR_BUS = PC_OUT ? PC_q : 8'bz;  // Controlled_Buffer controlled_buffer_2
  nand nand_1 (RESET, counter_1_q[0], counter_1_q[1]);
  // Probe on ADDR_BUS
  Counter #(.max('h7), .width(3)) counter_2 (
    .clr(or_1_out), .load(1'b0), .up(1'b1), .count(1'b1), .clk(CLK), .Q(counter_2_q[2:0]));  // open: D, carry
  or or_1 (or_1_out, RESET, RESET_CTR);
  // Probe on DATA_BUS
  Register IR (.D(DATA_BUS), .en(LOAD_IR), .clk(CLK), .Q(counter_2_q[11:4]), .clr(RESET));
  Adder adder_2 (.a(REGA_DATA), .b(REGB_DATA), .out(adder_2_out), .cout(CARRY));  // open: cin
  Subtractor subtractor_1 (.a(REGA_DATA), .b(REGB_DATA), .out(subtractor_1_out));  // open: bin, bout
  Multiplier multiplier_1 (.a(REGA_DATA), .b(REGB_DATA), .out(multiplier_1_out));  // open: cin, cout
  Divider divider_1 (.a(REGA_DATA), .b(REGB_DATA), .out(divider_1_out));  // open: upper, rem
  // Probe on {counter_2_q[11:4], 1'b0, counter_2_q[2:0]}
  PLA #(.in_width(12), .out_width(24), .\table ("xxxxxxxx0000 000000000100000000010010 # fetch\n000000010001 000000000000001000010101 # lda get ix\n000000010010 000000000000010000110001 # lda get ix ref data\n000000010011 000000001000000000000010 # lda done\n000000100001 000000000000001000010101 # ldb get ix\n000000100010 000000000000010010010001 # ldb get ix ref data\n000000100011 000000001000000000000010 # ldb done\n000000110001 000000000000001000010101 # sta get ix\n000000110010 000000000000010001001001 # sta set ix ref data\n000000110011 000000001000000000000010 # sta done\n000001000001 000000000000001000010101 # stb get ix\n000001000010 000000000000010100001001 # stb set ix ref data\n000001000011 000000001000000000000010 # stb done\n000001010001 000000000001100000100001 # add a + b\n000001010010 000000001000000000000010 # add done")) cpu_logic (
    .in({counter_2_q[11:4], 1'b0, counter_2_q[2:0]}),
    .out({ALU_MODE, cpu_logic_out[19:16], RESET_CTR, LOAD_IR, cpu_logic_out[13], LOAD_FLAGS, LOAD_ALU, IX_OUT, LOAD_IX, REGB_OUT, LOAD_REGB, REGA_OUT, LOAD_REGA, RAM_OE, RAM_WE, PCP1_OUT, PC_OUT, LOAD_PC}));
  Multiplexer #(.select(4), .width(8)) multiplexer_1 (
    .in0(adder_2_out), .in1(subtractor_1_out), .in2(multiplier_1_out), .in3(divider_1_out), .out(ALU_OUT),
    .sel(ALU_MODE));  // open: in4, in5, in6, in7, in8, in9, in10, in11, in12, in13, in14, in15
  // Probe on {ALU_MODE, cpu_logic_out[19:16], RESET_CTR, LOAD_IR, cpu_logic_out[13], LOAD_FLAGS, LOAD_ALU, IX_OUT, LOAD_IX, REGB_OUT, LOAD_REGB, REGA_OUT, LOAD_REGA, RAM_OE, RAM_WE, PCP1_OUT, PC_OUT, LOAD_PC}
  Comparator comparator_1 (.a({8{1'b0}}), .b(ALU_OUT), .eq(ZERO));  // open: gt, lt
  // Probe on ADDR_BUS
  RAM #(.trigger("falling"), .\type ("nonvolatile")) ram_1 (
    .addr(ADDR_BUS), .we(RAM_WE), .oe(RAM_OE), .clk(CLK), .din(DATA_BUS), .dout(ram_1_dout));
  Multiplexer #(.width(8)) multiplexer_2 (.in0(DATA_BUS), .in1(ALU_OUT), .out(multiplexer_2_out), .sel(LOAD_ALU));
  Register REGA (.D(multiplexer_2_out), .en(LOAD_REGA), .clk(CLK), .Q(REGA_DATA), .clr(RESET));
  Register REGB (.D(DATA_BUS), .en(LOAD_REGB), .clk(CLK), .Q(REGB_DATA), .clr(RESET));
  Register IX (.D(DATA_BUS), .en(LOAD_IX), .clk(CLK), .Q(IX_q), .clr(RESET));
  Register STATUS_FLAGS (.D({{6{1'b0}}, ZERO, CARRY}), .en(LOAD_FLAGS), .clk(CLK), .Q(STATUS_FLAGS_q), .clr(RESET));
  assign DATA_BUS = REGA_OUT ? REGA_DATA : 8'bz;  // Controlled_Buffer controlled_buffer_3
  assign DATA_BUS = REGB_OUT ? REGB_DATA : 8'bz;  // Controlled_Buffer controlled_buffer_4
  assign ADDR_BUS = IX_OUT ? IX_q : 8'bz;  // Controlled_Buffer controlled_buffer_5
  // Probe on ram_1_dout
  assign DATA_BUS = RAM_OE ? ram_1_dout : 8'bz;  // Controlled_Buffer controlled_buffer_6
endmodule
